// Logisim project ALU.circ as structural Verilog: 7 circuits, main circuit main
module main (
  input  A4,
  input  A3,
  input  A2,
  input  A1,
  input  B4,
  input  B3,
  input  B2,
  input  B1,
  input  CS2,
  input  CS1,
  input  CS0,
  output S4,
  output S3,
  output S2,
  output S1,
  output Z,
  output S,
  output V,
  output C
);

  wire a_pr_1_y1, a_pr_1_y2, a_pr_1_y3, a_pr_1_y4, b_pr_1_y1, b_pr_1_y2, b_pr_1_y3, b_pr_1_y4,
       logic_circuit_1_y1, logic_circuit_1_y2, logic_circuit_1_y3, logic_circuit_1_y4, n7402_1_p1,
       n7402_1_p4, n7402_1_p7, n7404_1_p2, n7404_1_p4, n7404_1_p5, n7432_1_p3, n7432_1_p6, n7432_1_p9,
       n7483_1_p2, n7483_1_p6, n7483_1_p10, n7483_1_p11, n7483_1_p16, n7486_1_p3, n7486_1_p6, n7486_1_p9;

  // _7404 7404_1: pin names not known; wires that end beside it: CS0, n7404_1_p2, CS1, n7404_1_p4, n7404_1_p5, Z
  // _7402 7402_1: pin names not known; wires that end beside it: n7402_1_p1, CS2, n7404_1_p2, n7402_1_p4, CS0, CS2, n7402_1_p7, CS2, CS1
  LOGIC_CIRCUIT logic_circuit_1 (
    .SELECTOR(CS0), .A4(A4), .A3(A3), .A2(A2), .A1(A1), .B4(B4), .B3(B3), .B2(B2), .B1(B1),
    .Y4(logic_circuit_1_y4), .Y3(logic_circuit_1_y3), .Y2(logic_circuit_1_y2), .Y1(logic_circuit_1_y1));
  A_PR a_pr_1 (
    .XOR_BIT(n7402_1_p4), .A4(A4), .A3(A3), .A2(A2), .A1(A1), .Y4(a_pr_1_y4), .Y3(a_pr_1_y3), .Y2(a_pr_1_y2),
    .Y1(a_pr_1_y1));
  B_PR b_pr_1 (
    .SELECTOR(n7402_1_p1), .CONST(CS2), .XOR_BIT(n7404_1_p4), .B4(B4), .B3(B3), .B2(B2), .B1(B1),
    .Y4(b_pr_1_y4), .Y3(b_pr_1_y3), .Y2(b_pr_1_y2), .Y1(b_pr_1_y1));
  // _7483 7483_1: pin names not known; wires that end beside it: a_pr_1_y4, n7483_1_p2, a_pr_1_y3, b_pr_1_y3, 1'b1, n7483_1_p6, b_pr_1_y2, a_pr_1_y2, b_pr_1_y4, n7483_1_p10, n7483_1_p11, n7402_1_p7, 1'b0, b_pr_1_y1, a_pr_1_y1, n7483_1_p16
  // _7432 7432_1: pin names not known; wires that end beside it: n7404_1_p4, n7402_1_p1, n7432_1_p3, S1, S2, n7432_1_p6, n7432_1_p6, S3, n7432_1_p9, n7432_1_p9, S, n7404_1_p5
  // _7486 7486_1: pin names not known; wires that end beside it: a_pr_1_y4, b_pr_1_y4, n7486_1_p3, n7486_1_p3, n7483_1_p11, n7486_1_p6, S, n7486_1_p6, n7486_1_p9
  _4_BIT_2X1_MUX u_4_bit_2x1_mux_1 (
    .A4(logic_circuit_1_y4), .A3(logic_circuit_1_y3), .A2(logic_circuit_1_y2), .A1(logic_circuit_1_y1),
    .L4(n7483_1_p10), .L3(n7483_1_p2), .L2(n7483_1_p6), .L1(n7483_1_p16), .SELECTOR(n7432_1_p3), .Y4(S),
    .Y3(S3), .Y2(S2), .Y1(S1));
  // _74157 74157_1: pin names not known; wires that end beside it: n7432_1_p3, 1'b0, n7486_1_p9, V, 1'b0, n7483_1_p11, C, 1'b0, 1'b0

  assign S4 = S;
endmodule

module _4_BIT_XOR (
  input  A4,
  input  A3,
  input  A2,
  input  A1,
  input  B4,
  input  B3,
  input  B2,
  input  B1,
  output Y4,
  output Y3,
  output Y2,
  output Y1
);

  // _7486 7486_1: pin names not known; wires that end beside it: A4, B4, Y4, A3, B3, Y3, A2, B2, Y2, A1, B1, Y1
endmodule

module _4_BIT_AND (
  input  A4,
  input  A3,
  input  A2,
  input  A1,
  input  B4,
  input  B3,
  input  B2,
  input  B1,
  output Y4,
  output Y3,
  output Y2,
  output Y1
);

  // _7408 7408_1: pin names not known; wires that end beside it: A4, B4, Y4, A3, B3, Y3, A2, B2, Y2, A1, B1, Y1
endmodule

// LOGICAL
module LOGIC_CIRCUIT (
  input  SELECTOR,
  input  A4,
  input  A3,
  input  A2,
  input  A1,
  input  B4,
  input  B3,
  input  B2,
  input  B1,
  output Y4,
  output Y3,
  output Y2,
  output Y1
);

  wire AND_y1, AND_y2, AND_y3, AND_y4, XOR_y1, XOR_y2, XOR_y3, XOR_y4;

  _4_BIT_XOR XOR (
    .A4(A4), .A3(A3), .A2(A2), .A1(A1), .B4(B4), .B3(B3), .B2(B2), .B1(B1), .Y4(XOR_y4), .Y3(XOR_y3),
    .Y2(XOR_y2), .Y1(XOR_y1));
  _4_BIT_AND AND (
    .A4(A4), .A3(A3), .A2(A2), .A1(A1), .B4(B4), .B3(B3), .B2(B2), .B1(B1), .Y4(AND_y4), .Y3(AND_y3),
    .Y2(AND_y2), .Y1(AND_y1));
  // _74157 74157_1: pin names not known; wires that end beside it: SELECTOR, XOR_y4, AND_y4, Y4, XOR_y3, AND_y3, Y3, 1'b0, XOR_y2, AND_y2, Y2, XOR_y1, AND_y1, Y1
endmodule

// X_i
module A_PR (
  input  XOR_BIT,
  input  A4,
  input  A3,
  input  A2,
  input  A1,
  output Y4,
  output Y3,
  output Y2,
  output Y1
);

  _4_BIT_XOR u_4_bit_xor_1 (
    .A4(A4), .A3(A3), .A2(A2), .A1(A1), .B4(XOR_BIT), .B3(XOR_BIT), .B2(XOR_BIT), .B1(XOR_BIT), .Y4(Y4),
    .Y3(Y3), .Y2(Y2), .Y1(Y1));
endmodule

// Y_i
module B_PR (
  input  SELECTOR,
  input  CONST,
  input  XOR_BIT,
  input  B4,
  input  B3,
  input  B2,
  input  B1,
  output Y4,
  output Y3,
  output Y2,
  output Y1
);

  wire n4_bit_xor_1_y1, n4_bit_xor_1_y2, n4_bit_xor_1_y3, n4_bit_xor_1_y4;

  _4_BIT_XOR u_4_bit_xor_1 (
    .A4(XOR_BIT), .A3(XOR_BIT), .A2(XOR_BIT), .A1(XOR_BIT), .B4(B4), .B3(B3), .B2(B2), .B1(B1),
    .Y4(n4_bit_xor_1_y4), .Y3(n4_bit_xor_1_y3), .Y2(n4_bit_xor_1_y2), .Y1(n4_bit_xor_1_y1));
  // _74157 74157_1: pin names not known; wires that end beside it: SELECTOR, CONST, n4_bit_xor_1_y4, Y4, CONST, n4_bit_xor_1_y3, Y3, 1'b0, CONST, n4_bit_xor_1_y2, Y2, CONST, n4_bit_xor_1_y1, Y1
endmodule

module _4_BIT_2X1_MUX (
  input  A4,
  input  A3,
  input  A2,
  input  A1,
  input  L4,
  input  L3,
  input  L2,
  input  L1,
  input  SELECTOR,
  output Y4,
  output Y3,
  output Y2,
  output Y1
);

  // _74157 74157_1: pin names not known; wires that end beside it: SELECTOR, A4, L4, Y4, A3, L3, Y3, 1'b0, 1'b1, 1'b0, A2, L2, Y2, A1, L1, Y1
endmodule
