// Logisim project Group_6.circ as structural Verilog: 5 circuits, main circuit main
module main (
  input  Clock,
  input  Reset,
  output [3:0] t0,
  output [3:0] t1,
  output [3:0] t2,
  output [3:0] t3,
  output [3:0] t4
);

  wire alu_1_zero_flag, control_1_alusrc, control_1_beq, control_1_bneq, control_1_jump, control_1_memread,
       control_1_memtoreg, control_1_memwrite, control_1_regdst, control_1_regwrite, multiplexer_3_out;
  wire [2:0] control_1_aluop;
  wire [3:0] alu_1_output, datamemory_1_data_read, multiplexer_1_out, multiplexer_4_out, multiplexer_6_out,
       register_1_read_data_1, register_1_read_data_2;
  wire [7:0] adder_1_out, adder_2_out, bit_extender_1_out, multiplexer_2_out, multiplexer_5_out, PC_q;
  wire [15:0] rom_1_data;

  Register_part #(.trigger("falling")) PC (.D(multiplexer_5_out), .Q(PC_q), .clk(Clock), .clr(Reset));  // open: en
  Adder adder_1 (.a(PC_q), .b(8'h1), .out(adder_1_out));  // open: cin, cout
  ROM #(.dataWidth(16)) rom_1 (.addr(PC_q), .data(rom_1_data), .sel(1'b1));
  assign bit_extender_1_out = {{4{rom_1_data[3]}}, rom_1_data[3:0]};  // Bit_Extender bit_extender_1
  Adder adder_2 (.a(bit_extender_1_out), .b(adder_1_out), .out(adder_2_out));  // open: cin, cout
  Control control_1 (
    .OP_Code(rom_1_data[15:12]), .ALUOp(control_1_aluop), .Jump(control_1_jump), .bneq(control_1_bneq),
    .beq(control_1_beq), .MemWrite(control_1_memwrite), .MemRead(control_1_memread),
    .RegWrite(control_1_regwrite), .MemToReg(control_1_memtoreg), .ALUSrc(control_1_alusrc),
    .RegDst(control_1_regdst));
  Multiplexer #(.width(4), .enable("false")) multiplexer_1 (
    .in0(rom_1_data[7:4]), .in1(rom_1_data[3:0]), .out(multiplexer_1_out), .sel(control_1_regdst));
  Multiplexer #(.width(8), .enable("false")) multiplexer_2 (
    .in0(adder_1_out), .in1(adder_2_out), .out(multiplexer_2_out), .sel(multiplexer_3_out));
  Multiplexer #(.enable("false")) multiplexer_3 (
    .in0(control_1_bneq), .in1(control_1_beq), .out(multiplexer_3_out), .sel(alu_1_zero_flag));
  Register register_1 (
    .Dst_Reg_1(multiplexer_1_out), .WriteData(multiplexer_6_out), .CLR(Reset), .SrcReg1(rom_1_data[11:8]),
    .SrcReg2(rom_1_data[7:4]), .RegWrite(control_1_regwrite), .CLK(Clock),
    .t4__t3__t2__t1__t0({t4, t3, t2, t1, t0}), .Read_Data_1(register_1_read_data_1),
    .Read_Data_2(register_1_read_data_2));
  Multiplexer #(.width(4), .enable("false")) multiplexer_4 (
    .in0(register_1_read_data_2), .in1(rom_1_data[3:0]), .out(multiplexer_4_out), .sel(control_1_alusrc));
  Multiplexer #(.width(8), .enable("false")) multiplexer_5 (
    .in0(multiplexer_2_out), .in1(rom_1_data[11:4]), .out(multiplexer_5_out), .sel(control_1_jump));
  ALU alu_1 (
    .ALUOp(control_1_aluop), .A(register_1_read_data_1), .B(multiplexer_4_out), .Output(alu_1_output),
    .Zero_flag(alu_1_zero_flag));
  DataMemory datamemory_1 (
    .Address(alu_1_output), .Write_Data(register_1_read_data_2), .MemWrite(control_1_memwrite),
    .MemRead(control_1_memread), .CLK(Clock), .CLR(Reset), .Data_Read(datamemory_1_data_read));
  // Probe on control_1_memwrite
  Multiplexer #(.width(4), .enable("false")) multiplexer_6 (
    .in0(alu_1_output), .in1(datamemory_1_data_read), .out(multiplexer_6_out), .sel(control_1_memtoreg));
  // Probe on control_1_memread

  // Notes on the sheet:
  //   write pc
  //   contents of rom_1 (hex, n*v repeats v):
  //   206f 2013 702e e127 6123 b724 5213 f221 8321 a1c0 1331 d224 5610 7661 5620 7661 a1a0 4727 9421 3115
  //   2661 d620 241 2661 d610 a1c0 8271 a110
  //   jump address
  //   write data
  //   mem to reg
endmodule

module Control (
  input  [3:0] OP_Code,
  output [2:0] ALUOp,
  output Jump,
  output bneq,
  output beq,
  output MemWrite,
  output MemRead,
  output RegWrite,
  output MemToReg,
  output ALUSrc,
  output RegDst
);

  ROM #(.addrWidth(4), .dataWidth(12)) rom_1 (
    .addr(OP_Code), .data({RegDst, ALUSrc, MemToReg, RegWrite, MemRead, MemWrite, beq, bneq, Jump, ALUOp}));  // open: sel

  // Notes on the sheet:
  //   contents of rom_1 (hex, n*v repeats v):
  //   11 502 8 506 780 503 904 903 500 501 901 440 900 902 505 21
endmodule

module Register (
  input  RegWrite,
  input  CLK,
  input  [3:0] Dst_Reg_1,
  input  [3:0] WriteData,
  input  CLR,
  input  [3:0] SrcReg1,
  input  [3:0] SrcReg2,
  output [19:0] t4__t3__t2__t1__t0,
  output [3:0] Read_Data_1,
  output [3:0] Read_Data_2
);

  wire and_1_out, demultiplexer_1_out1, demultiplexer_1_out2, demultiplexer_1_out3, demultiplexer_1_out4,
       demultiplexer_1_out5, demultiplexer_1_out6, not_1_out, not_2_out, not_3_out, not_4_out, not_5_out,
       not_6_out;
  wire [3:0] sp_q;

  not not_1 (not_1_out, demultiplexer_1_out2);
  Register_part #(.width(4)) t1 (.D(WriteData), .Q(t4__t3__t2__t1__t0[7:4]), .clk(not_1_out), .clr(CLR));  // open: en
  not not_2 (not_2_out, demultiplexer_1_out3);
  Register_part #(.width(4)) t2 (.D(WriteData), .Q(t4__t3__t2__t1__t0[11:8]), .clk(not_2_out), .clr(CLR));  // open: en
  Multiplexer #(.select(3), .width(4), .enable("false")) multiplexer_1 (
    .in0(4'b0000), .in1(t4__t3__t2__t1__t0[7:4]), .in2(t4__t3__t2__t1__t0[11:8]),
    .in3(t4__t3__t2__t1__t0[15:12]), .in4(t4__t3__t2__t1__t0[19:16]), .in5(4'b0000), .in6(sp_q),
    .in7(t4__t3__t2__t1__t0[3:0]), .out(Read_Data_1), .sel(SrcReg1[2:0]));
  Demultiplexer #(.select(3), .enable("false")) demultiplexer_1 (
    .out1(demultiplexer_1_out1), .out2(demultiplexer_1_out2), .out3(demultiplexer_1_out3),
    .out4(demultiplexer_1_out4), .out5(demultiplexer_1_out5), .out6(demultiplexer_1_out6), .in(and_1_out),
    .sel(Dst_Reg_1[2:0]));  // open: out0, out7
  not not_3 (not_3_out, demultiplexer_1_out4);
  Register_part #(.width(4)) t3 (.D(WriteData), .Q(t4__t3__t2__t1__t0[15:12]), .clk(not_3_out), .clr(CLR));  // open: en
  and and_1 (and_1_out, RegWrite, CLK);
  not not_4 (not_4_out, demultiplexer_1_out5);
  Register_part #(.width(4)) t4 (.D(WriteData), .Q(t4__t3__t2__t1__t0[19:16]), .clk(not_4_out), .clr(CLR));  // open: en
  Multiplexer #(.select(3), .width(4), .enable("false")) multiplexer_2 (
    .in0(4'b0000), .in1(t4__t3__t2__t1__t0[7:4]), .in2(t4__t3__t2__t1__t0[11:8]),
    .in3(t4__t3__t2__t1__t0[15:12]), .in4(t4__t3__t2__t1__t0[19:16]), .in5(4'b0000), .in6(sp_q),
    .in7(t4__t3__t2__t1__t0[3:0]), .out(Read_Data_2), .sel(SrcReg2[2:0]));
  not not_5 (not_5_out, demultiplexer_1_out1);
  Register_part #(.width(4)) t0 (.D(WriteData), .Q(t4__t3__t2__t1__t0[3:0]), .clk(not_5_out), .clr(CLR));  // open: en
  not not_6 (not_6_out, demultiplexer_1_out6);
  Register_part #(.width(4)) sp (.D(WriteData), .Q(sp_q), .clk(not_6_out), .clr(CLR));  // open: en

  // Notes on the sheet:
  //   $zero
endmodule

module ALU (
  input  [2:0] ALUOp,
  input  [3:0] A,
  input  [3:0] B,
  output [3:0] Output,
  output Zero_flag
);

  wire [3:0] adder_1_out, and_1_out, nor_1_out, or_1_out, shifter_1_out, shifter_2_out, subtractor_1_out;

  Adder #(.width(4)) adder_1 (.a(A), .b(B), .out(adder_1_out), .cin(1'b0));  // open: cout
  Subtractor #(.width(4)) subtractor_1 (.a(A), .b(B), .out(subtractor_1_out), .bin(1'b0));  // open: bout
  assign and_1_out = A & B;  // AND_Gate and_1, 4 bits wide
  assign or_1_out = A | B;  // OR_Gate or_1, 4 bits wide
  assign nor_1_out = ~(A | B);  // NOR_Gate nor_1, 4 bits wide
  Shifter #(.width(4)) shifter_1 (.in(A), .\dist (B[1:0]), .out(shifter_1_out));
  Shifter #(.width(4), .shift("lr")) shifter_2 (.in(A), .\dist (B[1:0]), .out(shifter_2_out));
  Multiplexer #(.select(3), .width(4), .enable("false")) multiplexer_1 (
    .in0(adder_1_out), .in1(subtractor_1_out), .in2(and_1_out), .in3(or_1_out), .in4(nor_1_out),
    .in5(shifter_1_out), .in6(shifter_2_out), .in7(4'b0000), .out(Output), .sel(ALUOp));
  nor nor_2 (Zero_flag, Output[0], Output[1], Output[2], Output[3]);
endmodule

module DataMemory (
  input  [3:0] Address,
  input  [3:0] Write_Data,
  input  MemWrite,
  input  MemRead,
  input  CLK,
  input  CLR,
  output [3:0] Data_Read
);

  wire not_1_out;

  not not_1 (not_1_out, CLK);
  RAM #(.addrWidth(4), .dataWidth(4), .bus("separate")) ram_1 (
    .addr(Address), .din(Write_Data), .data(Data_Read), .str(MemWrite), .clk(not_1_out), .ld(MemRead),
    .clr(CLR));  // open: sel
endmodule
