// Logisim project ALU.circ as structural Verilog: 4 circuits, main circuit main
module main (
  input  A4,
  input  A3,
  input  A2,
  input  A1,
  input  B4,
  input  B3,
  input  B2,
  input  B1,
  input  in_9,
  input  in_10,
  input  in_11
);
endmodule

module _4_BIT_XOR (
  input  A4,
  input  A3,
  input  A2,
  input  A1,
  input  B4,
  input  B3,
  input  B2,
  input  B1,
  output Y4,
  output Y3,
  output Y2,
  output Y1
);

  // _7486 7486_1: pin names not known; wires that end beside it: A4, B4, Y4, A3, B3, Y3, A2, B2, Y2, A1, B1, Y1
endmodule

module _4_BIT_AND (
  input  A4,
  input  A3,
  input  A2,
  input  A1,
  input  B4,
  input  B3,
  input  B2,
  input  B1,
  output Y4,
  output Y3,
  output Y2,
  output Y1
);

  // _7408 7408_1: pin names not known; wires that end beside it: A4, B4, Y4, A3, B3, Y3, A2, B2, Y2, A1, B1, Y1
endmodule

module LOGIC_CIRCUIT (
  input  SELECTOR,
  input  A4,
  input  A3,
  input  A2,
  input  A1,
  input  B4,
  input  B3,
  input  B2,
  input  B1,
  output Y4,
  output Y3,
  output Y2,
  output Y1
);

  wire AND_y1, AND_y2, AND_y3, AND_y4, XOR_y1, XOR_y2, XOR_y3, XOR_y4;

  _4_BIT_XOR XOR (
    .A4(A4), .A3(A3), .A2(A2), .A1(A1), .B4(B4), .B3(B3), .B2(B2), .B1(B1), .Y4(XOR_y4), .Y3(XOR_y3),
    .Y2(XOR_y2), .Y1(XOR_y1));
  _4_BIT_AND AND (
    .A4(A4), .A3(A3), .A2(A2), .A1(A1), .B4(B4), .B3(B3), .B2(B2), .B1(B1), .Y4(AND_y4), .Y3(AND_y3),
    .Y2(AND_y2), .Y1(AND_y1));
  // _74157 74157_1: pin names not known; wires that end beside it: SELECTOR, XOR_y4, AND_y4, Y4, XOR_y3, AND_y3, Y3, 1'b0, XOR_y2, AND_y2, Y2, XOR_y1, AND_y1, Y1
endmodule
